# Fritzing sketch project_1 (saved by Fritzing 0.9.2b)
breadboards: 1

parts:
  Part1 = Arduino Uno (Rev3)
  LED1 = LED - 5mm [color="Red (633nm)" package="5 mm [THT]"]
  R1 = Resistor [tolerance=±5% resistance=220 package=THT]
  R2 = Resistor [tolerance=±5% resistance=220 package=THT]
  R3 = Resistor [tolerance=±5% resistance=220 package=THT]
  R4 = Rotary Potentiometer (Small) [maximum_resistance=100kΩ package=THT]
  LED2 = LED - 5mm [color="Green (565nm)" package="5 mm [THT]"]
  LED3 = LED - 5mm [color="Green (565nm)" package="5 mm [THT]"]
  LED4 = LED - 5mm [color="Green (565nm)" package="5 mm [THT]"]
  LED5 = LED - 5mm [color="Green (565nm)" package="5 mm [THT]"]
  R5 = Resistor [tolerance=±5% resistance=220 package=THT]
  R6 = Resistor [tolerance=±5% resistance=220 package=THT]
  S1 = Pushbutton [package="[THT]"]
  S2 = Pushbutton [package="[THT]"]
  S3 = Pushbutton [package="[THT]"]
  S4 = Pushbutton [package="[THT]"]
  R7 = Resistor [tolerance=±5% resistance=10k package=THT]
  R9 = Resistor [tolerance=±5% resistance=10k package=THT]
  R10 = Resistor [tolerance=±5% resistance=10k package=THT]
  R8 = Resistor [tolerance=±5% resistance=2.2k package=THT]

nets:
  N1: Part1.A0, R4.wiper
  N2: Part1.D9_PWM, R1.Pin_1
  N3: Part1.D10_PWM/SS, R2.Pin_1
  N4: Part1.D11_PWM/MOSI, R3.Pin_1
  N5: Part1.D12/MISO, R5.Pin_1
  N6: Part1.D13/SCK, R6.Pin_1
  N7: Part1.D2, S1.Pin_3, S1.Pin_4, R7.Pin_1
  N8: Part1.D3_PWM, S2.Pin_3, S2.Pin_4, R8.Pin_1
  N9: Part1.D4, S3.Pin_3, S3.Pin_4, R9.Pin_1
  N10: Part1.D5_PWM, S4.Pin_3, S4.Pin_4, R10.Pin_1
  N11: Part1.5V, S1.Pin_1, S1.Pin_2, S2.Pin_1, S2.Pin_2, S3.Pin_1, S3.Pin_2, S4.Pin_1, S4.Pin_2
  N12: Part1.GND, LED1.cathode, R4.leg1, R4.leg2, LED2.cathode, LED3.cathode, LED4.cathode, LED5.cathode, R7.Pin_0, R9.Pin_0, R10.Pin_0, R8.Pin_0
  N13: LED1.anode, R1.Pin_0
  N14: R2.Pin_0, LED2.anode
  N15: R3.Pin_0, LED3.anode
  N16: LED4.anode, R5.Pin_0
  N17: LED5.anode, R6.Pin_0
